// Digital circuit comp.dig as structural Verilog
module comp (
  input  [7:0] a,
  input  [7:0] b,
  input  dir,
  output [7:0] aout,
  output [7:0] bout
);

  wire direction, go, swap;

  Comparator #(.Bits(8)) comparator_1 (.a(a), .b(b), .gt(swap));  // open: eq, lt
  Multiplexer multiplexer_1 (.sel(dir), .in_0(1'b0), .in_1(1'b1), .out(direction));
  Comparator comparator_2 (.a(swap), .b(direction), .eq(go));  // open: gt, lt
  Multiplexer #(.Bits(8)) multiplexer_2 (.sel(go), .in_0(a), .in_1(b), .out(aout));
  Multiplexer #(.Bits(8)) multiplexer_3 (.sel(go), .in_0(b), .in_1(a), .out(bout));
endmodule
