// Digital circuit sort1_rev.dig as structural Verilog
module sort1_rev (
  input  [7:0] x1,
  input  [7:0] x2,
  input  [7:0] x3,
  input  [7:0] x4,
  input  [7:0] x5,
  input  [7:0] x6,
  input  [7:0] x7,
  input  [7:0] x8,
  output [7:0] y1,
  output [7:0] y2,
  output [7:0] y3,
  output [7:0] y4,
  output [7:0] y5,
  output [7:0] y6,
  output [7:0] y7,
  output [7:0] y8
);

  wire [7:0] BN_2_aout, BN_2_bout, BN_3_aout, BN_3_bout, BN_4_aout, BN_4_bout, BN_5_aout, BN_5_bout,
       BN_6_aout, BN_6_bout, BN_7_aout, BN_7_bout, BN_8_aout, BN_8_bout, BN_9_aout, BN_9_bout, BN_10_aout,
       BN_10_bout, BN_11_aout, BN_11_bout, BN_12_aout, BN_12_bout, BN_13_aout, BN_13_bout, BN_14_aout,
       BN_14_bout, BN_15_aout, BN_15_bout, BN_16_aout, BN_16_bout, BN_17_aout, BN_17_bout, BN_18_aout,
       BN_18_bout, BN_19_aout, BN_19_bout, BN_20_aout, BN_20_bout, BN_aout, BN_bout;

  comp BN (.a(x1), .b(x2), .dir(1'b1), .aout(BN_aout), .bout(BN_bout));
  comp BN_2 (.a(x3), .b(x4), .dir(1'b0), .aout(BN_2_aout), .bout(BN_2_bout));
  comp BN_3 (.a(x5), .b(x6), .dir(1'b1), .aout(BN_3_aout), .bout(BN_3_bout));
  comp BN_4 (.a(x7), .b(x8), .dir(1'b0), .aout(BN_4_aout), .bout(BN_4_bout));
  comp BN_5 (.a(BN_aout), .b(BN_2_aout), .dir(1'b1), .aout(BN_5_aout), .bout(BN_5_bout));
  comp BN_6 (.a(BN_bout), .b(BN_2_bout), .dir(1'b1), .aout(BN_6_aout), .bout(BN_6_bout));
  comp BN_7 (.a(BN_3_aout), .b(BN_4_aout), .dir(1'b0), .aout(BN_7_aout), .bout(BN_7_bout));
  comp BN_8 (.a(BN_3_bout), .b(BN_4_bout), .dir(1'b0), .aout(BN_8_aout), .bout(BN_8_bout));
  comp BN_9 (.a(BN_5_aout), .b(BN_6_aout), .dir(1'b1), .aout(BN_9_aout), .bout(BN_9_bout));
  comp BN_10 (.a(BN_5_bout), .b(BN_6_bout), .dir(1'b1), .aout(BN_10_aout), .bout(BN_10_bout));
  comp BN_11 (.a(BN_7_aout), .b(BN_8_aout), .dir(1'b0), .aout(BN_11_aout), .bout(BN_11_bout));
  comp BN_12 (.a(BN_7_bout), .b(BN_8_bout), .dir(1'b0), .aout(BN_12_aout), .bout(BN_12_bout));
  comp BN_13 (.a(BN_9_aout), .b(BN_11_aout), .dir(1'b0), .aout(BN_13_aout), .bout(BN_13_bout));
  comp BN_14 (.a(BN_9_bout), .b(BN_11_bout), .dir(1'b0), .aout(BN_14_aout), .bout(BN_14_bout));
  comp BN_15 (.a(BN_10_aout), .b(BN_12_aout), .dir(1'b0), .aout(BN_15_aout), .bout(BN_15_bout));
  comp BN_16 (.a(BN_10_bout), .b(BN_12_bout), .dir(1'b0), .aout(BN_16_aout), .bout(BN_16_bout));
  comp BN_17 (.a(BN_13_aout), .b(BN_15_aout), .dir(1'b0), .aout(BN_17_aout), .bout(BN_17_bout));
  comp BN_18 (.a(BN_14_aout), .b(BN_16_aout), .dir(1'b0), .aout(BN_18_aout), .bout(BN_18_bout));
  comp BN_19 (.a(BN_13_bout), .b(BN_15_bout), .dir(1'b0), .aout(BN_19_aout), .bout(BN_19_bout));
  comp BN_20 (.a(BN_14_bout), .b(BN_16_bout), .dir(1'b0), .aout(BN_20_aout), .bout(BN_20_bout));
  comp BN_21 (.a(BN_17_aout), .b(BN_18_aout), .dir(1'b0), .aout(y1), .bout(y2));
  comp BN_22 (.a(BN_17_bout), .b(BN_18_bout), .dir(1'b0), .aout(y3), .bout(y4));
  comp BN_23 (.a(BN_19_aout), .b(BN_20_aout), .dir(1'b0), .aout(y5), .bout(y6));
  comp BN_24 (.a(BN_19_bout), .b(BN_20_bout), .dir(1'b0), .aout(y7), .bout(y8));
endmodule
