// Digital circuit sort4_rev.dig as structural Verilog
module sort4_rev (
  input  [7:0] x1,
  input  [7:0] x2,
  input  [7:0] x3,
  input  [7:0] x4,
  input  [7:0] x5,
  input  [7:0] x6,
  input  [7:0] x7,
  input  [7:0] x8,
  input  [7:0] x9,
  input  [7:0] x10,
  input  [7:0] x11,
  input  [7:0] x12,
  input  [7:0] x13,
  input  [7:0] x14,
  input  [7:0] x15,
  input  [7:0] x16,
  output [7:0] y1,
  output [7:0] y2,
  output [7:0] y3,
  output [7:0] y4,
  output [7:0] y5,
  output [7:0] y6,
  output [7:0] y7,
  output [7:0] y8,
  output [7:0] y9,
  output [7:0] y10,
  output [7:0] y11,
  output [7:0] y12,
  output [7:0] y13,
  output [7:0] y14,
  output [7:0] y15,
  output [7:0] y16
);

  wire [7:0] BN_2_aout, BN_2_bout, BN_3_aout, BN_3_bout, BN_4_aout, BN_4_bout, BN_5_aout, BN_5_bout,
       BN_6_aout, BN_6_bout, BN_7_aout, BN_7_bout, BN_8_aout, BN_8_bout, BN_9_aout, BN_9_bout, BN_10_aout,
       BN_10_bout, BN_11_aout, BN_11_bout, BN_12_aout, BN_12_bout, BN_13_aout, BN_13_bout, BN_14_aout,
       BN_14_bout, BN_15_aout, BN_15_bout, BN_16_aout, BN_16_bout, BN_17_aout, BN_17_bout, BN_18_aout,
       BN_18_bout, BN_19_aout, BN_19_bout, BN_20_aout, BN_20_bout, BN_21_aout, BN_21_bout, BN_22_aout,
       BN_22_bout, BN_23_aout, BN_23_bout, BN_24_aout, BN_24_bout, BN_aout, BN_bout, sort1_1_y1, sort1_1_y2,
       sort1_1_y3, sort1_1_y4, sort1_1_y5, sort1_1_y6, sort1_1_y7, sort1_1_y8, sort1_rev_1_y1,
       sort1_rev_1_y2, sort1_rev_1_y3, sort1_rev_1_y4, sort1_rev_1_y5, sort1_rev_1_y6, sort1_rev_1_y7,
       sort1_rev_1_y8;

  sort1 sort1_1 (
    .x1(x1), .x2(x2), .x3(x3), .x4(x4), .x5(x5), .x6(x6), .x7(x7), .x8(x8), .y1(sort1_1_y1), .y2(sort1_1_y2),
    .y3(sort1_1_y3), .y4(sort1_1_y4), .y5(sort1_1_y5), .y6(sort1_1_y6), .y7(sort1_1_y7), .y8(sort1_1_y8));
  sort1_rev sort1_rev_1 (
    .x1(x9), .x2(x10), .x3(x11), .x4(x12), .x5(x13), .x6(x14), .x7(x15), .x8(x16), .y1(sort1_rev_1_y1),
    .y2(sort1_rev_1_y2), .y3(sort1_rev_1_y3), .y4(sort1_rev_1_y4), .y5(sort1_rev_1_y5), .y6(sort1_rev_1_y6),
    .y7(sort1_rev_1_y7), .y8(sort1_rev_1_y8));
  comp BN (.a(sort1_1_y1), .b(sort1_rev_1_y1), .dir(1'b0), .aout(BN_aout), .bout(BN_bout));
  comp BN_2 (.a(sort1_1_y2), .b(sort1_rev_1_y2), .dir(1'b0), .aout(BN_2_aout), .bout(BN_2_bout));
  comp BN_3 (.a(sort1_1_y3), .b(sort1_rev_1_y3), .dir(1'b0), .aout(BN_3_aout), .bout(BN_3_bout));
  comp BN_4 (.a(sort1_1_y4), .b(sort1_rev_1_y4), .dir(1'b0), .aout(BN_4_aout), .bout(BN_4_bout));
  comp BN_5 (.a(sort1_1_y5), .b(sort1_rev_1_y5), .dir(1'b0), .aout(BN_5_aout), .bout(BN_5_bout));
  comp BN_6 (.a(sort1_1_y6), .b(sort1_rev_1_y6), .dir(1'b0), .aout(BN_6_aout), .bout(BN_6_bout));
  comp BN_7 (.a(sort1_1_y7), .b(sort1_rev_1_y7), .dir(1'b0), .aout(BN_7_aout), .bout(BN_7_bout));
  comp BN_8 (.a(sort1_1_y8), .b(sort1_rev_1_y8), .dir(1'b0), .aout(BN_8_aout), .bout(BN_8_bout));
  comp BN_9 (.a(BN_aout), .b(BN_5_aout), .dir(1'b0), .aout(BN_9_aout), .bout(BN_9_bout));
  comp BN_10 (.a(BN_2_aout), .b(BN_6_aout), .dir(1'b0), .aout(BN_10_aout), .bout(BN_10_bout));
  comp BN_11 (.a(BN_3_aout), .b(BN_7_aout), .dir(1'b0), .aout(BN_11_aout), .bout(BN_11_bout));
  comp BN_12 (.a(BN_4_aout), .b(BN_8_aout), .dir(1'b0), .aout(BN_12_aout), .bout(BN_12_bout));
  comp BN_13 (.a(BN_bout), .b(BN_5_bout), .dir(1'b0), .aout(BN_13_aout), .bout(BN_13_bout));
  comp BN_14 (.a(BN_2_bout), .b(BN_6_bout), .dir(1'b0), .aout(BN_14_aout), .bout(BN_14_bout));
  comp BN_15 (.a(BN_3_bout), .b(BN_7_bout), .dir(1'b0), .aout(BN_15_aout), .bout(BN_15_bout));
  comp BN_16 (.a(BN_4_bout), .b(BN_8_bout), .dir(1'b0), .aout(BN_16_aout), .bout(BN_16_bout));
  comp BN_17 (.a(BN_9_aout), .b(BN_11_aout), .dir(1'b0), .aout(BN_17_aout), .bout(BN_17_bout));
  comp BN_18 (.a(BN_10_aout), .b(BN_12_aout), .dir(1'b0), .aout(BN_18_aout), .bout(BN_18_bout));
  comp BN_19 (.a(BN_9_bout), .b(BN_11_bout), .dir(1'b0), .aout(BN_19_aout), .bout(BN_19_bout));
  comp BN_20 (.a(BN_10_bout), .b(BN_12_bout), .dir(1'b0), .aout(BN_20_aout), .bout(BN_20_bout));
  comp BN_21 (.a(BN_13_aout), .b(BN_15_aout), .dir(1'b0), .aout(BN_21_aout), .bout(BN_21_bout));
  comp BN_22 (.a(BN_14_aout), .b(BN_16_aout), .dir(1'b0), .aout(BN_22_aout), .bout(BN_22_bout));
  comp BN_23 (.a(BN_13_bout), .b(BN_15_bout), .dir(1'b0), .aout(BN_23_aout), .bout(BN_23_bout));
  comp BN_24 (.a(BN_14_bout), .b(BN_16_bout), .dir(1'b0), .aout(BN_24_aout), .bout(BN_24_bout));
  comp BN_25 (.a(BN_17_aout), .b(BN_18_aout), .dir(1'b0), .aout(y1), .bout(y2));
  comp BN_26 (.a(BN_17_bout), .b(BN_18_bout), .dir(1'b0), .aout(y3), .bout(y4));
  comp BN_27 (.a(BN_19_aout), .b(BN_20_aout), .dir(1'b0), .aout(y5), .bout(y6));
  comp BN_28 (.a(BN_19_bout), .b(BN_20_bout), .dir(1'b0), .aout(y7), .bout(y8));
  comp BN_29 (.a(BN_21_aout), .b(BN_22_aout), .dir(1'b0), .aout(y9), .bout(y10));
  comp BN_30 (.a(BN_21_bout), .b(BN_22_bout), .dir(1'b0), .aout(y11), .bout(y12));
  comp BN_31 (.a(BN_23_aout), .b(BN_24_aout), .dir(1'b0), .aout(y13), .bout(y14));
  comp BN_32 (.a(BN_23_bout), .b(BN_24_bout), .dir(1'b0), .aout(y15), .bout(y16));
endmodule

/* Test case:
x1 x2 x3 x4 x5 x6 x7 x8 x9 x10 x11 x12 x13 x14 x15 x16 y1 y2 y3 y4 y5 y6 y7 y8 y9 y10 y11 y12 y13 y14 y15 y16 
32 31 30 29 28 27 26 25 24 23 22 21 20 19 18 17 17 18 19 20 21 22 23 24 25 26 27 28 29 30 31 32
*/
