// Digital circuit sort5_rev.dig as structural Verilog
module sort5_rev (
  input  [7:0] x1,
  input  [7:0] x2,
  input  [7:0] x3,
  input  [7:0] x4,
  input  [7:0] x5,
  input  [7:0] x6,
  input  [7:0] x7,
  input  [7:0] x8,
  input  [7:0] x9,
  input  [7:0] x10,
  input  [7:0] x11,
  input  [7:0] x12,
  input  [7:0] x13,
  input  [7:0] x14,
  input  [7:0] x15,
  input  [7:0] x16,
  input  [7:0] x17,
  input  [7:0] x18,
  input  [7:0] x19,
  input  [7:0] x20,
  input  [7:0] x21,
  input  [7:0] x22,
  input  [7:0] x23,
  input  [7:0] x24,
  input  [7:0] x25,
  input  [7:0] x26,
  input  [7:0] x27,
  input  [7:0] x28,
  input  [7:0] x29,
  input  [7:0] x30,
  input  [7:0] x31,
  input  [7:0] x32,
  output [7:0] y1,
  output [7:0] y2,
  output [7:0] y3,
  output [7:0] y4,
  output [7:0] y5,
  output [7:0] y6,
  output [7:0] y7,
  output [7:0] y8,
  output [7:0] y9,
  output [7:0] y10,
  output [7:0] y11,
  output [7:0] y12,
  output [7:0] y13,
  output [7:0] y14,
  output [7:0] y15,
  output [7:0] y16,
  output [7:0] y17,
  output [7:0] y18,
  output [7:0] y19,
  output [7:0] y20,
  output [7:0] y21,
  output [7:0] y22,
  output [7:0] y23,
  output [7:0] y24,
  output [7:0] y25,
  output [7:0] y26,
  output [7:0] y27,
  output [7:0] y28,
  output [7:0] y29,
  output [7:0] y30,
  output [7:0] y31,
  output [7:0] y32
);

  wire [7:0] BN_2_aout, BN_2_bout, BN_3_aout, BN_3_bout, BN_4_aout, BN_4_bout, BN_5_aout, BN_5_bout,
       BN_6_aout, BN_6_bout, BN_7_aout, BN_7_bout, BN_8_aout, BN_8_bout, BN_9_aout, BN_9_bout, BN_10_aout,
       BN_10_bout, BN_11_aout, BN_11_bout, BN_12_aout, BN_12_bout, BN_13_aout, BN_13_bout, BN_14_aout,
       BN_14_bout, BN_15_aout, BN_15_bout, BN_16_aout, BN_16_bout, BN_17_aout, BN_17_bout, BN_18_aout,
       BN_18_bout, BN_19_aout, BN_19_bout, BN_20_aout, BN_20_bout, BN_21_aout, BN_21_bout, BN_22_aout,
       BN_22_bout, BN_23_aout, BN_23_bout, BN_24_aout, BN_24_bout, BN_25_aout, BN_25_bout, BN_26_aout,
       BN_26_bout, BN_27_aout, BN_27_bout, BN_28_aout, BN_28_bout, BN_29_aout, BN_29_bout, BN_30_aout,
       BN_30_bout, BN_31_aout, BN_31_bout, BN_32_aout, BN_32_bout, BN_33_aout, BN_33_bout, BN_34_aout,
       BN_34_bout, BN_35_aout, BN_35_bout, BN_36_aout, BN_36_bout, BN_37_aout, BN_37_bout, BN_38_aout,
       BN_38_bout, BN_39_aout, BN_39_bout, BN_40_aout, BN_40_bout, BN_41_aout, BN_41_bout, BN_42_aout,
       BN_42_bout, BN_43_aout, BN_43_bout, BN_44_aout, BN_44_bout, BN_45_aout, BN_45_bout, BN_46_aout,
       BN_46_bout, BN_47_aout, BN_47_bout, BN_48_aout, BN_48_bout, BN_49_aout, BN_49_bout, BN_50_aout,
       BN_50_bout, BN_51_aout, BN_51_bout, BN_52_aout, BN_52_bout, BN_53_aout, BN_53_bout, BN_54_aout,
       BN_54_bout, BN_55_aout, BN_55_bout, BN_56_aout, BN_56_bout, BN_57_aout, BN_57_bout, BN_58_aout,
       BN_58_bout, BN_59_aout, BN_59_bout, BN_60_aout, BN_60_bout, BN_61_aout, BN_61_bout, BN_62_aout,
       BN_62_bout, BN_63_aout, BN_63_bout, BN_64_aout, BN_64_bout, BN_aout, BN_bout, sort4_1_y1, sort4_1_y2,
       sort4_1_y3, sort4_1_y4, sort4_1_y5, sort4_1_y6, sort4_1_y7, sort4_1_y8, sort4_1_y9, sort4_1_y10,
       sort4_1_y11, sort4_1_y12, sort4_1_y13, sort4_1_y14, sort4_1_y15, sort4_1_y16, sort4_rev_1_y1,
       sort4_rev_1_y2, sort4_rev_1_y3, sort4_rev_1_y4, sort4_rev_1_y5, sort4_rev_1_y6, sort4_rev_1_y7,
       sort4_rev_1_y8, sort4_rev_1_y9, sort4_rev_1_y10, sort4_rev_1_y11, sort4_rev_1_y12, sort4_rev_1_y13,
       sort4_rev_1_y14, sort4_rev_1_y15, sort4_rev_1_y16;

  sort4 sort4_1 (
    .x1(x1), .x2(x2), .x3(x3), .x4(x4), .x5(x5), .x6(x6), .x7(x7), .x8(x8), .x9(x9), .x10(x10), .x11(x11),
    .x12(x12), .x13(x13), .x14(x14), .x15(x15), .x16(x16), .y1(sort4_1_y1), .y2(sort4_1_y2), .y3(sort4_1_y3),
    .y4(sort4_1_y4), .y5(sort4_1_y5), .y6(sort4_1_y6), .y7(sort4_1_y7), .y8(sort4_1_y8), .y9(sort4_1_y9),
    .y10(sort4_1_y10), .y11(sort4_1_y11), .y12(sort4_1_y12), .y13(sort4_1_y13), .y14(sort4_1_y14),
    .y15(sort4_1_y15), .y16(sort4_1_y16));
  sort4_rev sort4_rev_1 (
    .x1(x17), .x2(x18), .x3(x19), .x4(x20), .x5(x21), .x6(x22), .x7(x23), .x8(x24), .x9(x25), .x10(x26),
    .x11(x27), .x12(x28), .x13(x29), .x14(x30), .x15(x31), .x16(x32), .y1(sort4_rev_1_y1),
    .y2(sort4_rev_1_y2), .y3(sort4_rev_1_y3), .y4(sort4_rev_1_y4), .y5(sort4_rev_1_y5), .y6(sort4_rev_1_y6),
    .y7(sort4_rev_1_y7), .y8(sort4_rev_1_y8), .y9(sort4_rev_1_y9), .y10(sort4_rev_1_y10),
    .y11(sort4_rev_1_y11), .y12(sort4_rev_1_y12), .y13(sort4_rev_1_y13), .y14(sort4_rev_1_y14),
    .y15(sort4_rev_1_y15), .y16(sort4_rev_1_y16));
  comp BN (.a(sort4_1_y1), .b(sort4_rev_1_y1), .dir(1'b0), .aout(BN_aout), .bout(BN_bout));
  comp BN_2 (.a(sort4_1_y2), .b(sort4_rev_1_y2), .dir(1'b0), .aout(BN_2_aout), .bout(BN_2_bout));
  comp BN_3 (.a(sort4_1_y3), .b(sort4_rev_1_y3), .dir(1'b0), .aout(BN_3_aout), .bout(BN_3_bout));
  comp BN_4 (.a(sort4_1_y4), .b(sort4_rev_1_y4), .dir(1'b0), .aout(BN_4_aout), .bout(BN_4_bout));
  comp BN_5 (.a(sort4_1_y5), .b(sort4_rev_1_y5), .dir(1'b0), .aout(BN_5_aout), .bout(BN_5_bout));
  comp BN_6 (.a(sort4_1_y6), .b(sort4_rev_1_y6), .dir(1'b0), .aout(BN_6_aout), .bout(BN_6_bout));
  comp BN_7 (.a(sort4_1_y7), .b(sort4_rev_1_y7), .dir(1'b0), .aout(BN_7_aout), .bout(BN_7_bout));
  comp BN_8 (.a(sort4_1_y8), .b(sort4_rev_1_y8), .dir(1'b0), .aout(BN_8_aout), .bout(BN_8_bout));
  comp BN_9 (.a(sort4_1_y9), .b(sort4_rev_1_y9), .dir(1'b0), .aout(BN_9_aout), .bout(BN_9_bout));
  comp BN_10 (.a(sort4_1_y10), .b(sort4_rev_1_y10), .dir(1'b0), .aout(BN_10_aout), .bout(BN_10_bout));
  comp BN_11 (.a(sort4_1_y11), .b(sort4_rev_1_y11), .dir(1'b0), .aout(BN_11_aout), .bout(BN_11_bout));
  comp BN_12 (.a(sort4_1_y12), .b(sort4_rev_1_y12), .dir(1'b0), .aout(BN_12_aout), .bout(BN_12_bout));
  comp BN_13 (.a(sort4_1_y13), .b(sort4_rev_1_y13), .dir(1'b0), .aout(BN_13_aout), .bout(BN_13_bout));
  comp BN_14 (.a(sort4_1_y14), .b(sort4_rev_1_y14), .dir(1'b0), .aout(BN_14_aout), .bout(BN_14_bout));
  comp BN_15 (.a(sort4_1_y15), .b(sort4_rev_1_y15), .dir(1'b0), .aout(BN_15_aout), .bout(BN_15_bout));
  comp BN_16 (.a(sort4_1_y16), .b(sort4_rev_1_y16), .dir(1'b0), .aout(BN_16_aout), .bout(BN_16_bout));
  comp BN_17 (.a(BN_aout), .b(BN_9_aout), .dir(1'b0), .aout(BN_17_aout), .bout(BN_17_bout));
  comp BN_18 (.a(BN_2_aout), .b(BN_10_aout), .dir(1'b0), .aout(BN_18_aout), .bout(BN_18_bout));
  comp BN_19 (.a(BN_3_aout), .b(BN_11_aout), .dir(1'b0), .aout(BN_19_aout), .bout(BN_19_bout));
  comp BN_20 (.a(BN_4_aout), .b(BN_12_aout), .dir(1'b0), .aout(BN_20_aout), .bout(BN_20_bout));
  comp BN_21 (.a(BN_5_aout), .b(BN_13_aout), .dir(1'b0), .aout(BN_21_aout), .bout(BN_21_bout));
  comp BN_22 (.a(BN_6_aout), .b(BN_14_aout), .dir(1'b0), .aout(BN_22_aout), .bout(BN_22_bout));
  comp BN_23 (.a(BN_7_aout), .b(BN_15_aout), .dir(1'b0), .aout(BN_23_aout), .bout(BN_23_bout));
  comp BN_24 (.a(BN_8_aout), .b(BN_16_aout), .dir(1'b0), .aout(BN_24_aout), .bout(BN_24_bout));
  comp BN_25 (.a(BN_bout), .b(BN_9_bout), .dir(1'b0), .aout(BN_25_aout), .bout(BN_25_bout));
  comp BN_26 (.a(BN_2_bout), .b(BN_10_bout), .dir(1'b0), .aout(BN_26_aout), .bout(BN_26_bout));
  comp BN_27 (.a(BN_3_bout), .b(BN_11_bout), .dir(1'b0), .aout(BN_27_aout), .bout(BN_27_bout));
  comp BN_28 (.a(BN_4_bout), .b(BN_12_bout), .dir(1'b0), .aout(BN_28_aout), .bout(BN_28_bout));
  comp BN_29 (.a(BN_5_bout), .b(BN_13_bout), .dir(1'b0), .aout(BN_29_aout), .bout(BN_29_bout));
  comp BN_30 (.a(BN_6_bout), .b(BN_14_bout), .dir(1'b0), .aout(BN_30_aout), .bout(BN_30_bout));
  comp BN_31 (.a(BN_7_bout), .b(BN_15_bout), .dir(1'b0), .aout(BN_31_aout), .bout(BN_31_bout));
  comp BN_32 (.a(BN_8_bout), .b(BN_16_bout), .dir(1'b0), .aout(BN_32_aout), .bout(BN_32_bout));
  comp BN_33 (.a(BN_17_aout), .b(BN_21_aout), .dir(1'b0), .aout(BN_33_aout), .bout(BN_33_bout));
  comp BN_34 (.a(BN_18_aout), .b(BN_22_aout), .dir(1'b0), .aout(BN_34_aout), .bout(BN_34_bout));
  comp BN_35 (.a(BN_19_aout), .b(BN_23_aout), .dir(1'b0), .aout(BN_35_aout), .bout(BN_35_bout));
  comp BN_36 (.a(BN_20_aout), .b(BN_24_aout), .dir(1'b0), .aout(BN_36_aout), .bout(BN_36_bout));
  comp BN_37 (.a(BN_17_bout), .b(BN_21_bout), .dir(1'b0), .aout(BN_37_aout), .bout(BN_37_bout));
  comp BN_38 (.a(BN_18_bout), .b(BN_22_bout), .dir(1'b0), .aout(BN_38_aout), .bout(BN_38_bout));
  comp BN_39 (.a(BN_19_bout), .b(BN_23_bout), .dir(1'b0), .aout(BN_39_aout), .bout(BN_39_bout));
  comp BN_40 (.a(BN_20_bout), .b(BN_24_bout), .dir(1'b0), .aout(BN_40_aout), .bout(BN_40_bout));
  comp BN_41 (.a(BN_25_aout), .b(BN_29_aout), .dir(1'b0), .aout(BN_41_aout), .bout(BN_41_bout));
  comp BN_42 (.a(BN_26_aout), .b(BN_30_aout), .dir(1'b0), .aout(BN_42_aout), .bout(BN_42_bout));
  comp BN_43 (.a(BN_27_aout), .b(BN_31_aout), .dir(1'b0), .aout(BN_43_aout), .bout(BN_43_bout));
  comp BN_44 (.a(BN_28_aout), .b(BN_32_aout), .dir(1'b0), .aout(BN_44_aout), .bout(BN_44_bout));
  comp BN_45 (.a(BN_25_bout), .b(BN_29_bout), .dir(1'b0), .aout(BN_45_aout), .bout(BN_45_bout));
  comp BN_46 (.a(BN_26_bout), .b(BN_30_bout), .dir(1'b0), .aout(BN_46_aout), .bout(BN_46_bout));
  comp BN_47 (.a(BN_27_bout), .b(BN_31_bout), .dir(1'b0), .aout(BN_47_aout), .bout(BN_47_bout));
  comp BN_48 (.a(BN_28_bout), .b(BN_32_bout), .dir(1'b0), .aout(BN_48_aout), .bout(BN_48_bout));
  comp BN_49 (.a(BN_33_aout), .b(BN_35_aout), .dir(1'b0), .aout(BN_49_aout), .bout(BN_49_bout));
  comp BN_50 (.a(BN_34_aout), .b(BN_36_aout), .dir(1'b0), .aout(BN_50_aout), .bout(BN_50_bout));
  comp BN_51 (.a(BN_33_bout), .b(BN_35_bout), .dir(1'b0), .aout(BN_51_aout), .bout(BN_51_bout));
  comp BN_52 (.a(BN_34_bout), .b(BN_36_bout), .dir(1'b0), .aout(BN_52_aout), .bout(BN_52_bout));
  comp BN_53 (.a(BN_37_aout), .b(BN_39_aout), .dir(1'b0), .aout(BN_53_aout), .bout(BN_53_bout));
  comp BN_54 (.a(BN_38_aout), .b(BN_40_aout), .dir(1'b0), .aout(BN_54_aout), .bout(BN_54_bout));
  comp BN_55 (.a(BN_37_bout), .b(BN_39_bout), .dir(1'b0), .aout(BN_55_aout), .bout(BN_55_bout));
  comp BN_56 (.a(BN_38_bout), .b(BN_40_bout), .dir(1'b0), .aout(BN_56_aout), .bout(BN_56_bout));
  comp BN_57 (.a(BN_41_aout), .b(BN_43_aout), .dir(1'b0), .aout(BN_57_aout), .bout(BN_57_bout));
  comp BN_58 (.a(BN_42_aout), .b(BN_44_aout), .dir(1'b0), .aout(BN_58_aout), .bout(BN_58_bout));
  comp BN_59 (.a(BN_41_bout), .b(BN_43_bout), .dir(1'b0), .aout(BN_59_aout), .bout(BN_59_bout));
  comp BN_60 (.a(BN_42_bout), .b(BN_44_bout), .dir(1'b0), .aout(BN_60_aout), .bout(BN_60_bout));
  comp BN_61 (.a(BN_45_aout), .b(BN_47_aout), .dir(1'b0), .aout(BN_61_aout), .bout(BN_61_bout));
  comp BN_62 (.a(BN_46_aout), .b(BN_48_aout), .dir(1'b0), .aout(BN_62_aout), .bout(BN_62_bout));
  comp BN_63 (.a(BN_45_bout), .b(BN_47_bout), .dir(1'b0), .aout(BN_63_aout), .bout(BN_63_bout));
  comp BN_64 (.a(BN_46_bout), .b(BN_48_bout), .dir(1'b0), .aout(BN_64_aout), .bout(BN_64_bout));
  comp BN_65 (.a(BN_49_aout), .b(BN_50_aout), .dir(1'b0), .aout(y1), .bout(y2));
  comp BN_66 (.a(BN_49_bout), .b(BN_50_bout), .dir(1'b0), .aout(y3), .bout(y4));
  comp BN_67 (.a(BN_51_aout), .b(BN_52_aout), .dir(1'b0), .aout(y5), .bout(y6));
  comp BN_68 (.a(BN_51_bout), .b(BN_52_bout), .dir(1'b0), .aout(y7), .bout(y8));
  comp BN_69 (.a(BN_53_aout), .b(BN_54_aout), .dir(1'b0), .aout(y9), .bout(y10));
  comp BN_70 (.a(BN_53_bout), .b(BN_54_bout), .dir(1'b0), .aout(y11), .bout(y12));
  comp BN_71 (.a(BN_55_aout), .b(BN_56_aout), .dir(1'b0), .aout(y13), .bout(y14));
  comp BN_72 (.a(BN_55_bout), .b(BN_56_bout), .dir(1'b0), .aout(y15), .bout(y16));
  comp BN_73 (.a(BN_57_aout), .b(BN_58_aout), .dir(1'b0), .aout(y17), .bout(y18));
  comp BN_74 (.a(BN_57_bout), .b(BN_58_bout), .dir(1'b0), .aout(y19), .bout(y20));
  comp BN_75 (.a(BN_59_aout), .b(BN_60_aout), .dir(1'b0), .aout(y21), .bout(y22));
  comp BN_76 (.a(BN_59_bout), .b(BN_60_bout), .dir(1'b0), .aout(y23), .bout(y24));
  comp BN_77 (.a(BN_61_aout), .b(BN_62_aout), .dir(1'b0), .aout(y25), .bout(y26));
  comp BN_78 (.a(BN_61_bout), .b(BN_62_bout), .dir(1'b0), .aout(y27), .bout(y28));
  comp BN_79 (.a(BN_63_aout), .b(BN_64_aout), .dir(1'b0), .aout(y29), .bout(y30));
  comp BN_80 (.a(BN_63_bout), .b(BN_64_bout), .dir(1'b0), .aout(y31), .bout(y32));
endmodule

/* Test case:
x1 x2 x3 x4 x5 x6 x7 x8 x9 x10 x11 x12 x13 x14 x15 x16 x17 x18 x19 x20 x21 x22 x23 x24 x25 x26 x27 x28 x29 x30 x31 x32 y1 y2 y3 y4 y5 y6 y7 y8 y9 y10 y11 y12 y13 y14 y15 y16 y17 y18 y19 y20 y21 y22 y23 y24 y25 y26 y27 y28 y29 y30 y31 y32
32 31 30 29 28 27 26 25 24 23 22 21 20 19 18 17 16 15 14 13 12 11 10 9 8 7 6 5 4 3 2 1 1 2 3 4 5 6 7 8 9 10 11 12 13 14 15 16 17 18 19 20 21 22 23 24 25 26 27 28 29 30 31 32
*/
