// Digital circuit sort6.dig as structural Verilog
module sort6 (
  input  [7:0] x1,
  input  [7:0] x2,
  input  [7:0] x3,
  input  [7:0] x4,
  input  [7:0] x5,
  input  [7:0] x6,
  input  [7:0] x7,
  input  [7:0] x8,
  input  [7:0] x9,
  input  [7:0] x10,
  input  [7:0] x11,
  input  [7:0] x12,
  input  [7:0] x13,
  input  [7:0] x14,
  input  [7:0] x15,
  input  [7:0] x16,
  input  [7:0] x17,
  input  [7:0] x18,
  input  [7:0] x19,
  input  [7:0] x20,
  input  [7:0] x21,
  input  [7:0] x22,
  input  [7:0] x23,
  input  [7:0] x24,
  input  [7:0] x25,
  input  [7:0] x26,
  input  [7:0] x27,
  input  [7:0] x28,
  input  [7:0] x29,
  input  [7:0] x30,
  input  [7:0] x31,
  input  [7:0] x32,
  input  [7:0] x33,
  input  [7:0] x34,
  input  [7:0] x35,
  input  [7:0] x36,
  input  [7:0] x37,
  input  [7:0] x38,
  input  [7:0] x39,
  input  [7:0] x40,
  input  [7:0] x41,
  input  [7:0] x42,
  input  [7:0] x43,
  input  [7:0] x44,
  input  [7:0] x45,
  input  [7:0] x46,
  input  [7:0] x47,
  input  [7:0] x48,
  input  [7:0] x49,
  input  [7:0] x50,
  input  [7:0] x51,
  input  [7:0] x52,
  input  [7:0] x53,
  input  [7:0] x54,
  input  [7:0] x55,
  input  [7:0] x56,
  input  [7:0] x57,
  input  [7:0] x58,
  input  [7:0] x59,
  input  [7:0] x60,
  input  [7:0] x61,
  input  [7:0] x62,
  input  [7:0] x63,
  input  [7:0] x64,
  output [7:0] y1,
  output [7:0] y2,
  output [7:0] y3,
  output [7:0] y4,
  output [7:0] y5,
  output [7:0] y6,
  output [7:0] y7,
  output [7:0] y8,
  output [7:0] y9,
  output [7:0] y10,
  output [7:0] y11,
  output [7:0] y12,
  output [7:0] y13,
  output [7:0] y14,
  output [7:0] y15,
  output [7:0] y16,
  output [7:0] y17,
  output [7:0] y18,
  output [7:0] y19,
  output [7:0] y20,
  output [7:0] y21,
  output [7:0] y22,
  output [7:0] y23,
  output [7:0] y24,
  output [7:0] y25,
  output [7:0] y26,
  output [7:0] y27,
  output [7:0] y28,
  output [7:0] y29,
  output [7:0] y30,
  output [7:0] y31,
  output [7:0] y32,
  output [7:0] y33,
  output [7:0] y34,
  output [7:0] y35,
  output [7:0] y36,
  output [7:0] y37,
  output [7:0] y38,
  output [7:0] y39,
  output [7:0] y40,
  output [7:0] y41,
  output [7:0] y42,
  output [7:0] y43,
  output [7:0] y44,
  output [7:0] y45,
  output [7:0] y46,
  output [7:0] y47,
  output [7:0] y48,
  output [7:0] y49,
  output [7:0] y50,
  output [7:0] y51,
  output [7:0] y52,
  output [7:0] y53,
  output [7:0] y54,
  output [7:0] y55,
  output [7:0] y56,
  output [7:0] y57,
  output [7:0] y58,
  output [7:0] y59,
  output [7:0] y60,
  output [7:0] y61,
  output [7:0] y62,
  output [7:0] y63,
  output [7:0] y64
);

  wire [7:0] BN_2_aout, BN_2_bout, BN_3_aout, BN_3_bout, BN_4_aout, BN_4_bout, BN_5_aout, BN_5_bout,
       BN_6_aout, BN_6_bout, BN_7_aout, BN_7_bout, BN_8_aout, BN_8_bout, BN_9_aout, BN_9_bout, BN_10_aout,
       BN_10_bout, BN_11_aout, BN_11_bout, BN_12_aout, BN_12_bout, BN_13_aout, BN_13_bout, BN_14_aout,
       BN_14_bout, BN_15_aout, BN_15_bout, BN_16_aout, BN_16_bout, BN_17_aout, BN_17_bout, BN_18_aout,
       BN_18_bout, BN_19_aout, BN_19_bout, BN_20_aout, BN_20_bout, BN_21_aout, BN_21_bout, BN_22_aout,
       BN_22_bout, BN_23_aout, BN_23_bout, BN_24_aout, BN_24_bout, BN_25_aout, BN_25_bout, BN_26_aout,
       BN_26_bout, BN_27_aout, BN_27_bout, BN_28_aout, BN_28_bout, BN_29_aout, BN_29_bout, BN_30_aout,
       BN_30_bout, BN_31_aout, BN_31_bout, BN_32_aout, BN_32_bout, BN_aout, BN_bout, sort5_1_y1, sort5_1_y2,
       sort5_1_y3, sort5_1_y4, sort5_1_y5, sort5_1_y6, sort5_1_y7, sort5_1_y8, sort5_1_y9, sort5_1_y10,
       sort5_1_y11, sort5_1_y12, sort5_1_y13, sort5_1_y14, sort5_1_y15, sort5_1_y16, sort5_1_y17,
       sort5_1_y18, sort5_1_y19, sort5_1_y20, sort5_1_y21, sort5_1_y22, sort5_1_y23, sort5_1_y24,
       sort5_1_y25, sort5_1_y26, sort5_1_y27, sort5_1_y28, sort5_1_y29, sort5_1_y30, sort5_1_y31,
       sort5_1_y32, sort5_rev_1_y1, sort5_rev_1_y2, sort5_rev_1_y3, sort5_rev_1_y4, sort5_rev_1_y5,
       sort5_rev_1_y6, sort5_rev_1_y7, sort5_rev_1_y8, sort5_rev_1_y9, sort5_rev_1_y10, sort5_rev_1_y11,
       sort5_rev_1_y12, sort5_rev_1_y13, sort5_rev_1_y14, sort5_rev_1_y15, sort5_rev_1_y16, sort5_rev_1_y17,
       sort5_rev_1_y18, sort5_rev_1_y19, sort5_rev_1_y20, sort5_rev_1_y21, sort5_rev_1_y22, sort5_rev_1_y23,
       sort5_rev_1_y24, sort5_rev_1_y25, sort5_rev_1_y26, sort5_rev_1_y27, sort5_rev_1_y28, sort5_rev_1_y29,
       sort5_rev_1_y30, sort5_rev_1_y31, sort5_rev_1_y32;

  sort5 sort5_1 (
    .x1(x1), .x2(x2), .x3(x3), .x4(x4), .x5(x5), .x6(x6), .x7(x7), .x8(x8), .x9(x9), .x10(x10), .x11(x11),
    .x12(x12), .x13(x13), .x14(x14), .x15(x15), .x16(x16), .x17(x17), .x18(x18), .x19(x19), .x20(x20),
    .x21(x21), .x22(x22), .x23(x23), .x24(x24), .x25(x25), .x26(x26), .x27(x27), .x28(x28), .x29(x29),
    .x30(x30), .x31(x31), .x32(x32), .y1(sort5_1_y1), .y2(sort5_1_y2), .y3(sort5_1_y3), .y4(sort5_1_y4),
    .y5(sort5_1_y5), .y6(sort5_1_y6), .y7(sort5_1_y7), .y8(sort5_1_y8), .y9(sort5_1_y9), .y10(sort5_1_y10),
    .y11(sort5_1_y11), .y12(sort5_1_y12), .y13(sort5_1_y13), .y14(sort5_1_y14), .y15(sort5_1_y15),
    .y16(sort5_1_y16), .y17(sort5_1_y17), .y18(sort5_1_y18), .y19(sort5_1_y19), .y20(sort5_1_y20),
    .y21(sort5_1_y21), .y22(sort5_1_y22), .y23(sort5_1_y23), .y24(sort5_1_y24), .y25(sort5_1_y25),
    .y26(sort5_1_y26), .y27(sort5_1_y27), .y28(sort5_1_y28), .y29(sort5_1_y29), .y30(sort5_1_y30),
    .y31(sort5_1_y31), .y32(sort5_1_y32));
  sort5_rev sort5_rev_1 (
    .x1(x33), .x2(x34), .x3(x35), .x4(x36), .x5(x37), .x6(x38), .x7(x39), .x8(x40), .x9(x41), .x10(x42),
    .x11(x43), .x12(x44), .x13(x45), .x14(x46), .x15(x47), .x16(x48), .x17(x49), .x18(x50), .x19(x51),
    .x20(x52), .x21(x53), .x22(x54), .x23(x55), .x24(x56), .x25(x57), .x26(x58), .x27(x59), .x28(x60),
    .x29(x61), .x30(x62), .x31(x63), .x32(x64), .y1(sort5_rev_1_y1), .y2(sort5_rev_1_y2),
    .y3(sort5_rev_1_y3), .y4(sort5_rev_1_y4), .y5(sort5_rev_1_y5), .y6(sort5_rev_1_y6), .y7(sort5_rev_1_y7),
    .y8(sort5_rev_1_y8), .y9(sort5_rev_1_y9), .y10(sort5_rev_1_y10), .y11(sort5_rev_1_y11),
    .y12(sort5_rev_1_y12), .y13(sort5_rev_1_y13), .y14(sort5_rev_1_y14), .y15(sort5_rev_1_y15),
    .y16(sort5_rev_1_y16), .y17(sort5_rev_1_y17), .y18(sort5_rev_1_y18), .y19(sort5_rev_1_y19),
    .y20(sort5_rev_1_y20), .y21(sort5_rev_1_y21), .y22(sort5_rev_1_y22), .y23(sort5_rev_1_y23),
    .y24(sort5_rev_1_y24), .y25(sort5_rev_1_y25), .y26(sort5_rev_1_y26), .y27(sort5_rev_1_y27),
    .y28(sort5_rev_1_y28), .y29(sort5_rev_1_y29), .y30(sort5_rev_1_y30), .y31(sort5_rev_1_y31),
    .y32(sort5_rev_1_y32));
  comp BN (.a(sort5_1_y1), .b(sort5_rev_1_y1), .dir(1'b1), .aout(BN_aout), .bout(BN_bout));
  comp BN_2 (.a(sort5_1_y2), .b(sort5_rev_1_y2), .dir(1'b1), .aout(BN_2_aout), .bout(BN_2_bout));
  comp BN_3 (.a(sort5_1_y3), .b(sort5_rev_1_y3), .dir(1'b1), .aout(BN_3_aout), .bout(BN_3_bout));
  comp BN_4 (.a(sort5_1_y4), .b(sort5_rev_1_y4), .dir(1'b1), .aout(BN_4_aout), .bout(BN_4_bout));
  comp BN_5 (.a(sort5_1_y5), .b(sort5_rev_1_y5), .dir(1'b1), .aout(BN_5_aout), .bout(BN_5_bout));
  comp BN_6 (.a(sort5_1_y6), .b(sort5_rev_1_y6), .dir(1'b1), .aout(BN_6_aout), .bout(BN_6_bout));
  comp BN_7 (.a(sort5_1_y7), .b(sort5_rev_1_y7), .dir(1'b1), .aout(BN_7_aout), .bout(BN_7_bout));
  comp BN_8 (.a(sort5_1_y8), .b(sort5_rev_1_y8), .dir(1'b1), .aout(BN_8_aout), .bout(BN_8_bout));
  comp BN_9 (.a(sort5_1_y9), .b(sort5_rev_1_y9), .dir(1'b1), .aout(BN_9_aout), .bout(BN_9_bout));
  comp BN_10 (.a(sort5_1_y10), .b(sort5_rev_1_y10), .dir(1'b1), .aout(BN_10_aout), .bout(BN_10_bout));
  comp BN_11 (.a(sort5_1_y11), .b(sort5_rev_1_y11), .dir(1'b1), .aout(BN_11_aout), .bout(BN_11_bout));
  comp BN_12 (.a(sort5_1_y12), .b(sort5_rev_1_y12), .dir(1'b1), .aout(BN_12_aout), .bout(BN_12_bout));
  comp BN_13 (.a(sort5_1_y13), .b(sort5_rev_1_y13), .dir(1'b1), .aout(BN_13_aout), .bout(BN_13_bout));
  comp BN_14 (.a(sort5_1_y14), .b(sort5_rev_1_y14), .dir(1'b1), .aout(BN_14_aout), .bout(BN_14_bout));
  comp BN_15 (.a(sort5_1_y15), .b(sort5_rev_1_y15), .dir(1'b1), .aout(BN_15_aout), .bout(BN_15_bout));
  comp BN_16 (.a(sort5_1_y16), .b(sort5_rev_1_y16), .dir(1'b1), .aout(BN_16_aout), .bout(BN_16_bout));
  comp BN_17 (.a(sort5_1_y17), .b(sort5_rev_1_y17), .dir(1'b1), .aout(BN_17_aout), .bout(BN_17_bout));
  comp BN_18 (.a(sort5_1_y18), .b(sort5_rev_1_y18), .dir(1'b1), .aout(BN_18_aout), .bout(BN_18_bout));
  comp BN_19 (.a(sort5_1_y19), .b(sort5_rev_1_y19), .dir(1'b1), .aout(BN_19_aout), .bout(BN_19_bout));
  comp BN_20 (.a(sort5_1_y20), .b(sort5_rev_1_y20), .dir(1'b1), .aout(BN_20_aout), .bout(BN_20_bout));
  comp BN_21 (.a(sort5_1_y21), .b(sort5_rev_1_y21), .dir(1'b1), .aout(BN_21_aout), .bout(BN_21_bout));
  comp BN_22 (.a(sort5_1_y22), .b(sort5_rev_1_y22), .dir(1'b1), .aout(BN_22_aout), .bout(BN_22_bout));
  comp BN_23 (.a(sort5_1_y23), .b(sort5_rev_1_y23), .dir(1'b1), .aout(BN_23_aout), .bout(BN_23_bout));
  comp BN_24 (.a(sort5_1_y24), .b(sort5_rev_1_y24), .dir(1'b1), .aout(BN_24_aout), .bout(BN_24_bout));
  comp BN_25 (.a(sort5_1_y25), .b(sort5_rev_1_y25), .dir(1'b1), .aout(BN_25_aout), .bout(BN_25_bout));
  comp BN_26 (.a(sort5_1_y26), .b(sort5_rev_1_y26), .dir(1'b1), .aout(BN_26_aout), .bout(BN_26_bout));
  comp BN_27 (.a(sort5_1_y27), .b(sort5_rev_1_y27), .dir(1'b1), .aout(BN_27_aout), .bout(BN_27_bout));
  comp BN_28 (.a(sort5_1_y28), .b(sort5_rev_1_y28), .dir(1'b1), .aout(BN_28_aout), .bout(BN_28_bout));
  comp BN_29 (.a(sort5_1_y29), .b(sort5_rev_1_y29), .dir(1'b1), .aout(BN_29_aout), .bout(BN_29_bout));
  comp BN_30 (.a(sort5_1_y30), .b(sort5_rev_1_y30), .dir(1'b1), .aout(BN_30_aout), .bout(BN_30_bout));
  comp BN_31 (.a(sort5_1_y31), .b(sort5_rev_1_y31), .dir(1'b1), .aout(BN_31_aout), .bout(BN_31_bout));
  comp BN_32 (.a(sort5_1_y32), .b(sort5_rev_1_y32), .dir(1'b1), .aout(BN_32_aout), .bout(BN_32_bout));
  sort5 sort5_2 (
    .x1(BN_aout), .x2(BN_17_aout), .x3(BN_2_aout), .x4(BN_18_aout), .x5(BN_3_aout), .x6(BN_19_aout),
    .x7(BN_4_aout), .x8(BN_20_aout), .x9(BN_5_aout), .x10(BN_21_aout), .x11(BN_6_aout), .x12(BN_22_aout),
    .x13(BN_7_aout), .x14(BN_23_aout), .x15(BN_8_aout), .x16(BN_24_aout), .x17(BN_9_aout), .x18(BN_25_aout),
    .x19(BN_10_aout), .x20(BN_26_aout), .x21(BN_11_aout), .x22(BN_27_aout), .x23(BN_12_aout),
    .x24(BN_28_aout), .x25(BN_13_aout), .x26(BN_29_aout), .x27(BN_14_aout), .x28(BN_30_aout),
    .x29(BN_15_aout), .x30(BN_31_aout), .x31(BN_16_aout), .x32(BN_32_aout), .y1(y1), .y2(y2), .y3(y3),
    .y4(y4), .y5(y5), .y6(y6), .y7(y7), .y8(y8), .y9(y9), .y10(y10), .y11(y11), .y12(y12), .y13(y13),
    .y14(y14), .y15(y15), .y16(y16), .y17(y17), .y18(y18), .y19(y19), .y20(y20), .y21(y21), .y22(y22),
    .y23(y23), .y24(y24), .y25(y25), .y26(y26), .y27(y27), .y28(y28), .y29(y29), .y30(y30), .y31(y31),
    .y32(y32));
  sort5 sort5_3 (
    .x1(BN_17_bout), .x2(BN_bout), .x3(BN_18_bout), .x4(BN_2_bout), .x5(BN_19_bout), .x6(BN_3_bout),
    .x7(BN_20_bout), .x8(BN_4_bout), .x9(BN_21_bout), .x10(BN_5_bout), .x11(BN_22_bout), .x12(BN_6_bout),
    .x13(BN_23_bout), .x14(BN_7_bout), .x15(BN_24_bout), .x16(BN_8_bout), .x17(BN_25_bout), .x18(BN_9_bout),
    .x19(BN_26_bout), .x20(BN_10_bout), .x21(BN_27_bout), .x22(BN_11_bout), .x23(BN_28_bout),
    .x24(BN_12_bout), .x25(BN_29_bout), .x26(BN_13_bout), .x27(BN_30_bout), .x28(BN_14_bout),
    .x29(BN_31_bout), .x30(BN_15_bout), .x31(BN_32_bout), .x32(BN_16_bout), .y1(y33), .y2(y34), .y3(y35),
    .y4(y36), .y5(y37), .y6(y38), .y7(y39), .y8(y40), .y9(y41), .y10(y42), .y11(y43), .y12(y44), .y13(y45),
    .y14(y46), .y15(y47), .y16(y48), .y17(y49), .y18(y50), .y19(y51), .y20(y52), .y21(y53), .y22(y54),
    .y23(y55), .y24(y56), .y25(y57), .y26(y58), .y27(y59), .y28(y60), .y29(y61), .y30(y62), .y31(y63),
    .y32(y64));
endmodule
