// Digital circuit sort7_rev.dig as structural Verilog
module sort7_rev (
  input  [7:0] x1,
  input  [7:0] x2,
  input  [7:0] x3,
  input  [7:0] x4,
  input  [7:0] x5,
  input  [7:0] x6,
  input  [7:0] x7,
  input  [7:0] x8,
  input  [7:0] x9,
  input  [7:0] x10,
  input  [7:0] x11,
  input  [7:0] x12,
  input  [7:0] x13,
  input  [7:0] x14,
  input  [7:0] x15,
  input  [7:0] x16,
  input  [7:0] x17,
  input  [7:0] x18,
  input  [7:0] x19,
  input  [7:0] x20,
  input  [7:0] x21,
  input  [7:0] x22,
  input  [7:0] x23,
  input  [7:0] x24,
  input  [7:0] x25,
  input  [7:0] x26,
  input  [7:0] x27,
  input  [7:0] x28,
  input  [7:0] x29,
  input  [7:0] x30,
  input  [7:0] x31,
  input  [7:0] x32,
  input  [7:0] x33,
  input  [7:0] x34,
  input  [7:0] x35,
  input  [7:0] x36,
  input  [7:0] x37,
  input  [7:0] x38,
  input  [7:0] x39,
  input  [7:0] x40,
  input  [7:0] x41,
  input  [7:0] x42,
  input  [7:0] x43,
  input  [7:0] x44,
  input  [7:0] x45,
  input  [7:0] x46,
  input  [7:0] x47,
  input  [7:0] x48,
  input  [7:0] x49,
  input  [7:0] x50,
  input  [7:0] x51,
  input  [7:0] x52,
  input  [7:0] x53,
  input  [7:0] x54,
  input  [7:0] x55,
  input  [7:0] x56,
  input  [7:0] x57,
  input  [7:0] x58,
  input  [7:0] x59,
  input  [7:0] x60,
  input  [7:0] x61,
  input  [7:0] x62,
  input  [7:0] x63,
  input  [7:0] x64,
  input  [7:0] x65,
  input  [7:0] x66,
  input  [7:0] x67,
  input  [7:0] x68,
  input  [7:0] x69,
  input  [7:0] x70,
  input  [7:0] x71,
  input  [7:0] x72,
  input  [7:0] x73,
  input  [7:0] x74,
  input  [7:0] x75,
  input  [7:0] x76,
  input  [7:0] x77,
  input  [7:0] x78,
  input  [7:0] x79,
  input  [7:0] x80,
  input  [7:0] x81,
  input  [7:0] x82,
  input  [7:0] x83,
  input  [7:0] x84,
  input  [7:0] x85,
  input  [7:0] x86,
  input  [7:0] x87,
  input  [7:0] x88,
  input  [7:0] x89,
  input  [7:0] x90,
  input  [7:0] x91,
  input  [7:0] x92,
  input  [7:0] x93,
  input  [7:0] x94,
  input  [7:0] x95,
  input  [7:0] x96,
  input  [7:0] x97,
  input  [7:0] x98,
  input  [7:0] x99,
  input  [7:0] x100,
  input  [7:0] x101,
  input  [7:0] x102,
  input  [7:0] x103,
  input  [7:0] x104,
  input  [7:0] x105,
  input  [7:0] x106,
  input  [7:0] x107,
  input  [7:0] x108,
  input  [7:0] x109,
  input  [7:0] x110,
  input  [7:0] x111,
  input  [7:0] x112,
  input  [7:0] x113,
  input  [7:0] x114,
  input  [7:0] x115,
  input  [7:0] x116,
  input  [7:0] x117,
  input  [7:0] x118,
  input  [7:0] x119,
  input  [7:0] x120,
  input  [7:0] x121,
  input  [7:0] x122,
  input  [7:0] x123,
  input  [7:0] x124,
  input  [7:0] x125,
  input  [7:0] x126,
  input  [7:0] x127,
  input  [7:0] x128,
  output [7:0] y1,
  output [7:0] y2,
  output [7:0] y3,
  output [7:0] y4,
  output [7:0] y5,
  output [7:0] y6,
  output [7:0] y7,
  output [7:0] y8,
  output [7:0] y9,
  output [7:0] y10,
  output [7:0] y11,
  output [7:0] y12,
  output [7:0] y13,
  output [7:0] y14,
  output [7:0] y15,
  output [7:0] y16,
  output [7:0] y17,
  output [7:0] y18,
  output [7:0] y19,
  output [7:0] y20,
  output [7:0] y21,
  output [7:0] y22,
  output [7:0] y23,
  output [7:0] y24,
  output [7:0] y25,
  output [7:0] y26,
  output [7:0] y27,
  output [7:0] y28,
  output [7:0] y29,
  output [7:0] y30,
  output [7:0] y31,
  output [7:0] y32,
  output [7:0] y33,
  output [7:0] y34,
  output [7:0] y35,
  output [7:0] y36,
  output [7:0] y37,
  output [7:0] y38,
  output [7:0] y39,
  output [7:0] y40,
  output [7:0] y41,
  output [7:0] y42,
  output [7:0] y43,
  output [7:0] y44,
  output [7:0] y45,
  output [7:0] y46,
  output [7:0] y47,
  output [7:0] y48,
  output [7:0] y49,
  output [7:0] y50,
  output [7:0] y51,
  output [7:0] y52,
  output [7:0] y53,
  output [7:0] y54,
  output [7:0] y55,
  output [7:0] y56,
  output [7:0] y57,
  output [7:0] y58,
  output [7:0] y59,
  output [7:0] y60,
  output [7:0] y61,
  output [7:0] y62,
  output [7:0] y63,
  output [7:0] y64,
  output [7:0] y65,
  output [7:0] y66,
  output [7:0] y67,
  output [7:0] y68,
  output [7:0] y69,
  output [7:0] y70,
  output [7:0] y71,
  output [7:0] y72,
  output [7:0] y73,
  output [7:0] y74,
  output [7:0] y75,
  output [7:0] y76,
  output [7:0] y77,
  output [7:0] y78,
  output [7:0] y79,
  output [7:0] y80,
  output [7:0] y81,
  output [7:0] y82,
  output [7:0] y83,
  output [7:0] y84,
  output [7:0] y85,
  output [7:0] y86,
  output [7:0] y87,
  output [7:0] y88,
  output [7:0] y89,
  output [7:0] y90,
  output [7:0] y91,
  output [7:0] y92,
  output [7:0] y93,
  output [7:0] y94,
  output [7:0] y95,
  output [7:0] y96,
  output [7:0] y97,
  output [7:0] y98,
  output [7:0] y99,
  output [7:0] y100,
  output [7:0] y101,
  output [7:0] y102,
  output [7:0] y103,
  output [7:0] y104,
  output [7:0] y105,
  output [7:0] y106,
  output [7:0] y107,
  output [7:0] y108,
  output [7:0] y109,
  output [7:0] y110,
  output [7:0] y111,
  output [7:0] y112,
  output [7:0] y113,
  output [7:0] y114,
  output [7:0] y115,
  output [7:0] y116,
  output [7:0] y117,
  output [7:0] y118,
  output [7:0] y119,
  output [7:0] y120,
  output [7:0] y121,
  output [7:0] y122,
  output [7:0] y123,
  output [7:0] y124,
  output [7:0] y125,
  output [7:0] y126,
  output [7:0] y127,
  output [7:0] y128
);

  wire [7:0] a1, a2, a3, a4, a5, a6, a7, a8, a9, a10, a11, a12, a13, a14, a15, a16, a17, a18, a19, a20, a21,
       a22, a23, a24, a25, a26, a27, a28, a29, a30, a31, a32, a33, a34, a35, a36, a37, a38, a39, a40, a41,
       a42, a43, a44, a45, a46, a47, a48, a49, a50, a51, a52, a53, a54, a55, a56, a57, a58, a59, a60, a61,
       a62, a63, a64, a65, a66, a67, a68, a69, a70, a71, a72, a73, a74, a75, a76, a77, a78, a79, a80, a81,
       a82, a83, a84, a85, a86, a87, a88, a89, a90, a91, a92, a93, a94, a95, a96, a97, a98, a99, a100, a101,
       a102, a103, a104, a105, a106, a107, a108, a109, a110, a111, a112, a113, a114, a115, a116, a117, a118,
       a119, a120, a121, a122, a123, a124, a125, a126, a127, a128, b1, b2, b3, b4, b5, b6, b7, b8, b9, b10,
       b11, b12, b13, b14, b15, b16, b17, b18, b19, b20, b21, b22, b23, b24, b25, b26, b27, b28, b29, b30,
       b31, b32, b33, b34, b35, b36, b37, b38, b39, b40, b41, b42, b43, b44, b45, b46, b47, b48, b49, b50,
       b51, b52, b53, b54, b55, b56, b57, b58, b59, b60, b61, b62, b63, b64, b65, b66, b67, b68, b69, b70,
       b71, b72, b73, b74, b75, b76, b77, b78, b79, b80, b81, b82, b83, b84, b85, b86, b87, b88, b89, b90,
       b91, b92, b93, b94, b95, b96, b97, b98, b99, b100, b101, b102, b103, b104, b105, b106, b107, b108,
       b109, b110, b111, b112, b113, b114, b115, b116, b117, b118, b119, b120, b121, b122, b123, b124, b125,
       b126, b127, b128;

  sort6 sort6_1 (
    .x1(x1), .x2(x2), .x3(x3), .x4(x4), .x5(x5), .x6(x6), .x7(x7), .x8(x8), .x9(x9), .x10(x10), .x11(x11),
    .x12(x12), .x13(x13), .x14(x14), .x15(x15), .x16(x16), .x17(x17), .x18(x18), .x19(x19), .x20(x20),
    .x21(x21), .x22(x22), .x23(x23), .x24(x24), .x25(x25), .x26(x26), .x27(x27), .x28(x28), .x29(x29),
    .x30(x30), .x31(x31), .x32(x32), .x33(x33), .x34(x34), .x35(x35), .x36(x36), .x37(x37), .x38(x38),
    .x39(x39), .x40(x40), .x41(x41), .x42(x42), .x43(x43), .x44(x44), .x45(x45), .x46(x46), .x47(x47),
    .x48(x48), .x49(x49), .x50(x50), .x51(x51), .x52(x52), .x53(x53), .x54(x54), .x55(x55), .x56(x56),
    .x57(x57), .x58(x58), .x59(x59), .x60(x60), .x61(x61), .x62(x62), .x63(x63), .x64(x64), .y1(a1), .y2(a2),
    .y3(a3), .y4(a4), .y5(a5), .y6(a6), .y7(a7), .y8(a8), .y9(a9), .y10(a10), .y11(a11), .y12(a12),
    .y13(a13), .y14(a14), .y15(a15), .y16(a16), .y17(a17), .y18(a18), .y19(a19), .y20(a20), .y21(a21),
    .y22(a22), .y23(a23), .y24(a24), .y25(a25), .y26(a26), .y27(a27), .y28(a28), .y29(a29), .y30(a30),
    .y31(a31), .y32(a32), .y33(a33), .y34(a34), .y35(a35), .y36(a36), .y37(a37), .y38(a38), .y39(a39),
    .y40(a40), .y41(a41), .y42(a42), .y43(a43), .y44(a44), .y45(a45), .y46(a46), .y47(a47), .y48(a48),
    .y49(a49), .y50(a50), .y51(a51), .y52(a52), .y53(a53), .y54(a54), .y55(a55), .y56(a56), .y57(a57),
    .y58(a58), .y59(a59), .y60(a60), .y61(a61), .y62(a62), .y63(a63), .y64(a64));
  sort6_rev sort6_rev_1 (
    .x1(x65), .x2(x66), .x3(x67), .x4(x68), .x5(x69), .x6(x70), .x7(x71), .x8(x72), .x9(x73), .x10(x74),
    .x11(x75), .x12(x76), .x13(x77), .x14(x78), .x15(x79), .x16(x80), .x17(x81), .x18(x82), .x19(x83),
    .x20(x84), .x21(x85), .x22(x86), .x23(x87), .x24(x88), .x25(x89), .x26(x90), .x27(x91), .x28(x92),
    .x29(x93), .x30(x94), .x31(x95), .x32(x96), .x33(x97), .x34(x98), .x35(x99), .x36(x100), .x37(x101),
    .x38(x102), .x39(x103), .x40(x104), .x41(x105), .x42(x106), .x43(x107), .x44(x108), .x45(x109),
    .x46(x110), .x47(x111), .x48(x112), .x49(x113), .x50(x114), .x51(x115), .x52(x116), .x53(x117),
    .x54(x118), .x55(x119), .x56(x120), .x57(x121), .x58(x122), .x59(x123), .x60(x124), .x61(x125),
    .x62(x126), .x63(x127), .x64(x128), .y1(a65), .y2(a66), .y3(a67), .y4(a68), .y5(a69), .y6(a70), .y7(a71),
    .y8(a72), .y9(a73), .y10(a74), .y11(a75), .y12(a76), .y13(a77), .y14(a78), .y15(a79), .y16(a80),
    .y17(a81), .y18(a82), .y19(a83), .y20(a84), .y21(a85), .y22(a86), .y23(a87), .y24(a88), .y25(a89),
    .y26(a90), .y27(a91), .y28(a92), .y29(a93), .y30(a94), .y31(a95), .y32(a96), .y33(a97), .y34(a98),
    .y35(a99), .y36(a100), .y37(a101), .y38(a102), .y39(a103), .y40(a104), .y41(a105), .y42(a106),
    .y43(a107), .y44(a108), .y45(a109), .y46(a110), .y47(a111), .y48(a112), .y49(a113), .y50(a114),
    .y51(a115), .y52(a116), .y53(a117), .y54(a118), .y55(a119), .y56(a120), .y57(a121), .y58(a122),
    .y59(a123), .y60(a124), .y61(a125), .y62(a126), .y63(a127), .y64(a128));
  comp BN (.a(a1), .b(a65), .dir(1'b1), .aout(b1), .bout(b2));
  comp BN_2 (.a(a2), .b(a66), .dir(1'b1), .aout(b3), .bout(b4));
  comp BN_3 (.a(a3), .b(a67), .dir(1'b1), .aout(b5), .bout(b6));
  comp BN_4 (.a(a4), .b(a68), .dir(1'b1), .aout(b7), .bout(b8));
  comp BN_5 (.a(a5), .b(a69), .dir(1'b1), .aout(b9), .bout(b10));
  comp BN_6 (.a(a6), .b(a70), .dir(1'b1), .aout(b11), .bout(b12));
  comp BN_7 (.a(a7), .b(a71), .dir(1'b1), .aout(b13), .bout(b14));
  comp BN_8 (.a(a8), .b(a72), .dir(1'b1), .aout(b15), .bout(b16));
  comp BN_9 (.a(a9), .b(a73), .dir(1'b1), .aout(b17), .bout(b18));
  comp BN_10 (.a(a10), .b(a74), .dir(1'b1), .aout(b19), .bout(b20));
  comp BN_11 (.a(a11), .b(a75), .dir(1'b1), .aout(b21), .bout(b22));
  comp BN_12 (.a(a12), .b(a76), .dir(1'b1), .aout(b23), .bout(b24));
  comp BN_13 (.a(a13), .b(a77), .dir(1'b1), .aout(b25), .bout(b26));
  comp BN_14 (.a(a14), .b(a78), .dir(1'b1), .aout(b27), .bout(b28));
  comp BN_15 (.a(a15), .b(a79), .dir(1'b1), .aout(b29), .bout(b30));
  comp BN_16 (.a(a16), .b(a80), .dir(1'b1), .aout(b31), .bout(b32));
  comp BN_17 (.a(a17), .b(a81), .dir(1'b1), .aout(b33), .bout(b34));
  comp BN_18 (.a(a18), .b(a82), .dir(1'b1), .aout(b35), .bout(b36));
  comp BN_19 (.a(a19), .b(a83), .dir(1'b1), .aout(b37), .bout(b38));
  comp BN_20 (.a(a20), .b(a84), .dir(1'b1), .aout(b39), .bout(b40));
  comp BN_21 (.a(a21), .b(a85), .dir(1'b1), .aout(b41), .bout(b42));
  comp BN_22 (.a(a22), .b(a86), .dir(1'b1), .aout(b43), .bout(b44));
  comp BN_23 (.a(a23), .b(a87), .dir(1'b1), .aout(b45), .bout(b46));
  comp BN_24 (.a(a24), .b(a88), .dir(1'b1), .aout(b47), .bout(b48));
  comp BN_25 (.a(a25), .b(a89), .dir(1'b1), .aout(b49), .bout(b50));
  comp BN_26 (.a(a26), .b(a90), .dir(1'b1), .aout(b51), .bout(b52));
  comp BN_27 (.a(a27), .b(a91), .dir(1'b1), .aout(b53), .bout(b54));
  comp BN_28 (.a(a28), .b(a92), .dir(1'b1), .aout(b55), .bout(b56));
  comp BN_29 (.a(a29), .b(a93), .dir(1'b1), .aout(b57), .bout(b58));
  comp BN_30 (.a(a30), .b(a94), .dir(1'b1), .aout(b59), .bout(b60));
  comp BN_31 (.a(a31), .b(a95), .dir(1'b1), .aout(b61), .bout(b62));
  comp BN_32 (.a(a32), .b(a96), .dir(1'b1), .aout(b63), .bout(b64));
  comp BN_33 (.a(a33), .b(a97), .dir(1'b1), .aout(b65), .bout(b66));
  comp BN_34 (.a(a34), .b(a98), .dir(1'b1), .aout(b67), .bout(b68));
  comp BN_35 (.a(a35), .b(a99), .dir(1'b1), .aout(b69), .bout(b70));
  comp BN_36 (.a(a36), .b(a100), .dir(1'b1), .aout(b71), .bout(b72));
  comp BN_37 (.a(a37), .b(a101), .dir(1'b1), .aout(b73), .bout(b74));
  comp BN_38 (.a(a38), .b(a102), .dir(1'b1), .aout(b75), .bout(b76));
  comp BN_39 (.a(a39), .b(a103), .dir(1'b1), .aout(b77), .bout(b78));
  comp BN_40 (.a(a40), .b(a104), .dir(1'b1), .aout(b79), .bout(b80));
  comp BN_41 (.a(a41), .b(a105), .dir(1'b1), .aout(b81), .bout(b82));
  comp BN_42 (.a(a42), .b(a106), .dir(1'b1), .aout(b83), .bout(b84));
  comp BN_43 (.a(a43), .b(a107), .dir(1'b1), .aout(b85), .bout(b86));
  comp BN_44 (.a(a44), .b(a108), .dir(1'b1), .aout(b87), .bout(b88));
  comp BN_45 (.a(a45), .b(a109), .dir(1'b1), .aout(b89), .bout(b90));
  comp BN_46 (.a(a46), .b(a110), .dir(1'b1), .aout(b91), .bout(b92));
  comp BN_47 (.a(a47), .b(a111), .dir(1'b1), .aout(b93), .bout(b94));
  comp BN_48 (.a(a48), .b(a112), .dir(1'b1), .aout(b95), .bout(b96));
  comp BN_49 (.a(a49), .b(a113), .dir(1'b1), .aout(b97), .bout(b98));
  comp BN_50 (.a(a50), .b(a114), .dir(1'b1), .aout(b99), .bout(b100));
  comp BN_51 (.a(a51), .b(a115), .dir(1'b1), .aout(b101), .bout(b102));
  comp BN_52 (.a(a52), .b(a116), .dir(1'b1), .aout(b103), .bout(b104));
  comp BN_53 (.a(a53), .b(a117), .dir(1'b1), .aout(b105), .bout(b106));
  comp BN_54 (.a(a54), .b(a118), .dir(1'b1), .aout(b107), .bout(b108));
  comp BN_55 (.a(a55), .b(a119), .dir(1'b1), .aout(b109), .bout(b110));
  comp BN_56 (.a(a56), .b(a120), .dir(1'b1), .aout(b111), .bout(b112));
  comp BN_57 (.a(a57), .b(a121), .dir(1'b1), .aout(b113), .bout(b114));
  comp BN_58 (.a(a58), .b(a122), .dir(1'b1), .aout(b115), .bout(b116));
  comp BN_59 (.a(a59), .b(a123), .dir(1'b1), .aout(b117), .bout(b118));
  comp BN_60 (.a(a60), .b(a124), .dir(1'b1), .aout(b119), .bout(b120));
  comp BN_61 (.a(a61), .b(a125), .dir(1'b1), .aout(b121), .bout(b122));
  comp BN_62 (.a(a62), .b(a126), .dir(1'b1), .aout(b123), .bout(b124));
  comp BN_63 (.a(a63), .b(a127), .dir(1'b1), .aout(b125), .bout(b126));
  comp BN_64 (.a(a64), .b(a128), .dir(1'b1), .aout(b127), .bout(b128));
  sort6 sort6_2 (
    .x1(b1), .x2(b65), .x3(b3), .x4(b67), .x5(b5), .x6(b69), .x7(b7), .x8(b71), .x9(b9), .x10(b73),
    .x11(b11), .x12(b75), .x13(b13), .x14(b77), .x15(b15), .x16(b79), .x17(b17), .x18(b81), .x19(b19),
    .x20(b83), .x21(b21), .x22(b85), .x23(b23), .x24(b87), .x25(b25), .x26(b89), .x27(b27), .x28(b91),
    .x29(b29), .x30(b93), .x31(b31), .x32(b95), .x33(b33), .x34(b97), .x35(b35), .x36(b99), .x37(b37),
    .x38(b101), .x39(b39), .x40(b103), .x41(b41), .x42(b105), .x43(b43), .x44(b107), .x45(b45), .x46(b109),
    .x47(b47), .x48(b111), .x49(b49), .x50(b113), .x51(b51), .x52(b115), .x53(b53), .x54(b117), .x55(b55),
    .x56(b119), .x57(b57), .x58(b121), .x59(b59), .x60(b123), .x61(b61), .x62(b125), .x63(b63), .x64(b127),
    .y1(y128), .y2(y127), .y3(y126), .y4(y125), .y5(y124), .y6(y123), .y7(y122), .y8(y121), .y9(y120),
    .y10(y119), .y11(y118), .y12(y117), .y13(y116), .y14(y115), .y15(y114), .y16(y113), .y17(y112),
    .y18(y111), .y19(y110), .y20(y109), .y21(y108), .y22(y107), .y23(y106), .y24(y105), .y25(y104),
    .y26(y103), .y27(y102), .y28(y101), .y29(y100), .y30(y99), .y31(y98), .y32(y97), .y33(y96), .y34(y95),
    .y35(y94), .y36(y93), .y37(y92), .y38(y91), .y39(y90), .y40(y89), .y41(y88), .y42(y87), .y43(y86),
    .y44(y85), .y45(y84), .y46(y83), .y47(y82), .y48(y81), .y49(y80), .y50(y79), .y51(y78), .y52(y77),
    .y53(y76), .y54(y75), .y55(y74), .y56(y73), .y57(y72), .y58(y71), .y59(y70), .y60(y69), .y61(y68),
    .y62(y67), .y63(y66), .y64(y65));
  sort6 sort6_3 (
    .x1(b2), .x2(b66), .x3(b4), .x4(b68), .x5(b6), .x6(b70), .x7(b8), .x8(b72), .x9(b10), .x10(b74),
    .x11(b12), .x12(b76), .x13(b14), .x14(b78), .x15(b16), .x16(b80), .x17(b18), .x18(b82), .x19(b20),
    .x20(b84), .x21(b22), .x22(b86), .x23(b24), .x24(b88), .x25(b26), .x26(b90), .x27(b28), .x28(b92),
    .x29(b30), .x30(b94), .x31(b32), .x32(b96), .x33(b34), .x34(b98), .x35(b36), .x36(b100), .x37(b38),
    .x38(b102), .x39(b40), .x40(b104), .x41(b42), .x42(b106), .x43(b44), .x44(b108), .x45(b46), .x46(b110),
    .x47(b48), .x48(b112), .x49(b50), .x50(b114), .x51(b52), .x52(b116), .x53(b54), .x54(b118), .x55(b56),
    .x56(b120), .x57(b58), .x58(b122), .x59(b60), .x60(b124), .x61(b62), .x62(b126), .x63(b64), .x64(b128),
    .y1(y64), .y2(y63), .y3(y62), .y4(y61), .y5(y60), .y6(y59), .y7(y58), .y8(y57), .y9(y56), .y10(y55),
    .y11(y54), .y12(y53), .y13(y52), .y14(y51), .y15(y50), .y16(y49), .y17(y48), .y18(y47), .y19(y46),
    .y20(y45), .y21(y44), .y22(y43), .y23(y42), .y24(y41), .y25(y40), .y26(y39), .y27(y38), .y28(y37),
    .y29(y36), .y30(y35), .y31(y34), .y32(y33), .y33(y32), .y34(y31), .y35(y30), .y36(y29), .y37(y28),
    .y38(y27), .y39(y26), .y40(y25), .y41(y24), .y42(y23), .y43(y22), .y44(y21), .y45(y20), .y46(y19),
    .y47(y18), .y48(y17), .y49(y16), .y50(y15), .y51(y14), .y52(y13), .y53(y12), .y54(y11), .y55(y10),
    .y56(y9), .y57(y8), .y58(y7), .y59(y6), .y60(y5), .y61(y4), .y62(y3), .y63(y2), .y64(y1));

  // Other names for the same wires on the sheet: y1_t[7:0] = y128; y2_t[7:0] = y127; y3_t[7:0] = y126;
  //   y4_t[7:0] = y125; y5_t[7:0] = y124; y6_t[7:0] = y123; y7_t[7:0] = y122; y8_t[7:0] = y121; y9_t[7:0] = y120;
  //   y10_t[7:0] = y119; y11_t[7:0] = y118; y12_t[7:0] = y117; y13_t[7:0] = y116; y14_t[7:0] = y115;
  //   y15_t[7:0] = y114; y16_t[7:0] = y113; y17_t[7:0] = y112; y18_t[7:0] = y111; y19_t[7:0] = y110;
  //   y20_t[7:0] = y109; y21_t[7:0] = y108; y22_t[7:0] = y107; y23_t[7:0] = y106; y24_t[7:0] = y105;
  //   y25_t[7:0] = y104; y26_t[7:0] = y103; y27_t[7:0] = y102; y28_t[7:0] = y101; y29_t[7:0] = y100; y30_t[7:0] = y99;
  //   y31_t[7:0] = y98; y32_t[7:0] = y97; y33_t[7:0] = y96; y34_t[7:0] = y95; y35_t[7:0] = y94; y36_t[7:0] = y93;
  //   y37_t[7:0] = y92; y38_t[7:0] = y91; y39_t[7:0] = y90; y40_t[7:0] = y89; y41_t[7:0] = y88; y42_t[7:0] = y87;
  //   y43_t[7:0] = y86; y44_t[7:0] = y85; y45_t[7:0] = y84; y46_t[7:0] = y83; y47_t[7:0] = y82; y48_t[7:0] = y81;
  //   y49_t[7:0] = y80; y50_t[7:0] = y79; y51_t[7:0] = y78; y52_t[7:0] = y77; y53_t[7:0] = y76; y54_t[7:0] = y75;
  //   y55_t[7:0] = y74; y56_t[7:0] = y73; y57_t[7:0] = y72; y58_t[7:0] = y71; y59_t[7:0] = y70; y60_t[7:0] = y69;
  //   y61_t[7:0] = y68; y62_t[7:0] = y67; y63_t[7:0] = y66; y64_t[7:0] = y65; y65_t[7:0] = y64; y66_t[7:0] = y63;
  //   y67_t[7:0] = y62; y68_t[7:0] = y61; y69_t[7:0] = y60; y70_t[7:0] = y59; y71_t[7:0] = y58; y72_t[7:0] = y57;
  //   y73_t[7:0] = y56; y74_t[7:0] = y55; y75_t[7:0] = y54; y76_t[7:0] = y53; y77_t[7:0] = y52; y78_t[7:0] = y51;
  //   y79_t[7:0] = y50; y80_t[7:0] = y49; y81_t[7:0] = y48; y82_t[7:0] = y47; y83_t[7:0] = y46; y84_t[7:0] = y45;
  //   y85_t[7:0] = y44; y86_t[7:0] = y43; y87_t[7:0] = y42; y88_t[7:0] = y41; y89_t[7:0] = y40; y90_t[7:0] = y39;
  //   y91_t[7:0] = y38; y92_t[7:0] = y37; y93_t[7:0] = y36; y94_t[7:0] = y35; y95_t[7:0] = y34; y96_t[7:0] = y33;
  //   y97_t[7:0] = y32; y98_t[7:0] = y31; y99_t[7:0] = y30; y100_t[7:0] = y29; y101_t[7:0] = y28; y102_t[7:0] = y27;
  //   y103_t[7:0] = y26; y104_t[7:0] = y25; y105_t[7:0] = y24; y106_t[7:0] = y23; y107_t[7:0] = y22;
  //   y108_t[7:0] = y21; y109_t[7:0] = y20; y110_t[7:0] = y19; y111_t[7:0] = y18; y112_t[7:0] = y17;
  //   y113_t[7:0] = y16; y114_t[7:0] = y15; y115_t[7:0] = y14; y116_t[7:0] = y13; y117_t[7:0] = y12;
  //   y118_t[7:0] = y11; y119_t[7:0] = y10; y120_t[7:0] = y9; y121_t[7:0] = y8; y122_t[7:0] = y7; y123_t[7:0] = y6;
  //   y124_t[7:0] = y5; y125_t[7:0] = y4; y126_t[7:0] = y3; y127_t[7:0] = y2; y128_t[7:0] = y1
endmodule
